# Fritzing sketch Devre (saved by Fritzing 0.9.6b)
breadboards: 1

parts:
  WeMos_D1_Mini1 = WeMos D1 Mini
  J1 = Piezo Speaker
  R1 = Photocell (LDR) [package=THT]
  PIR1 = PIR sensor
  RHT1 = Humidity and Temperature Sensor RHT03
  R2 = Resistor [tolerance=±5% resistance=10k package="0603 [SMD]"]

nets:
  5V: WeMos_D1_Mini1.5V, R1.pin_0, PIR1.VDD, RHT1.Vcc
  N1: WeMos_D1_Mini1.A0, R1.pin_1, R2.Pin_0
  N2: WeMos_D1_Mini1.D2, PIR1.SIG
  N3: WeMos_D1_Mini1.D4, RHT1.Data-signal
  N4: WeMos_D1_Mini1.D7, J1.pin2
  N5: WeMos_D1_Mini1.G, J1.pin1, PIR1.GND, RHT1.GND_2, R2.Pin_1
